# Fritzing sketch LCD_Arrangement (saved by Fritzing 0.9.3b)
breadboards: 1

parts:
  U1 = LCD-16X2 [package=lcd-16x2_noholes]
  R1 = Rotary Potentiometer (Small) [maximum_resistance=100kΩ package=THT]
  R2 = Resistor [tolerance=±5% resistance=220 package=THT]
  Part1 = Arduino Uno (Rev3)

nets:
  VSS: U1.VSS, U1.K, R1.leg2, R2.Pin_1, Part1.GND
  VDD: U1.VDD, R1.leg1, Part1.5V
  N1: U1.VO, R1.wiper
  N2: U1.RS, Part1.D11_PWM/MOSI
  N3: U1.R_W, Part1.D10_PWM/SS
  N4: U1.E, Part1.D9_PWM
  N5: U1.DB4, Part1.D5_PWM
  N6: U1.DB5, Part1.D4
  N7: U1.DB6, Part1.D3_PWM
  N8: U1.DB7, Part1.D2
  N9: U1.A, R2.Pin_0
